# Fritzing sketch LED_grid (saved by Fritzing 0.9.3b)

parts:
  Adafruit_3444 = Adafruit 3444 [part_number="Adafruit #3444"]
  C1 = Electrolytic Capacitor [capacitance=220µF package="100 mil [THT, electrolytic]"]  # not connected
  Part1 = Adafruit Perma-Proto HAT [part_number="Adafruit #2314 and #2310"]
  Raspberry_Pi_1 = Raspberry Pi 3 [part_number=RPI-3-V1.2]
  CONN1 = USB connector [package=THT]
  U1 = 74AHCT125 [part_number=SN74AHCT125 package=dil14]

nets:
  N1: Adafruit_3444.CIN, Part1.N$56, U1.2Y
  N2: Adafruit_3444.DIN, Part1.N$54, U1.1Y
  GND: Adafruit_3444.GND, Part1.GND, Part1.N$7, Part1.N$8, Part1.N$10, Part1.N$11, Part1.N$51, Part1.N$53, Part1.N$57, Raspberry_Pi_1.GND, CONN1.GND, CONN1.chassis5, CONN1.chassis6, U1.1OE, U1.2OE, U1.GND, U1.3A, U1.3OE, U1.4A, U1.4OE
  N3: Adafruit_3444.VDD, Part1.N$12#214
  N4: Part1.SDA, Raspberry_Pi_1.GPIO2
  N5: Part1.SCL, Raspberry_Pi_1.GPIO3
  N6: Part1.TXD, Raspberry_Pi_1.GPIO14
  N7: Part1.GPIO4, Raspberry_Pi_1.GPIO4
  N8: Part1.GPIO18, Raspberry_Pi_1.GPIO18
  N9: Part1.GPIO24, Raspberry_Pi_1.GPIO24
  N10: Part1.SPI_MOSI, Part1.N$52, Raspberry_Pi_1.GPIO10, U1.1A
  N11: Part1.SPI_SCLK, Part1.N$49#311, Part1.N$55#344, Raspberry_Pi_1.GPIO11, U1.2A
  N12: Part1.SPI_CE1, Raspberry_Pi_1.GPIO7
  N13: Part1.GPIO6, Raspberry_Pi_1.GPIO6
  N14: Part1.GPIO13, Raspberry_Pi_1.GPIO13
  3V3: Part1.3.3V, Raspberry_Pi_1.3v3, Raspberry_Pi_1.3V3
  N15: Part1.5.0V, Raspberry_Pi_1.5V
  N16: Part1.RXD, Raspberry_Pi_1.GPIO15
  N17: Part1.GPIO17, Raspberry_Pi_1.GPIO17
  N18: Part1.GPIO27, Raspberry_Pi_1.GPIO27
  N19: Part1.GPIO22, Raspberry_Pi_1.GPIO22
  N20: Part1.GPIO23, Raspberry_Pi_1.GPIO23
  N21: Part1.SPI_MISO, Raspberry_Pi_1.GPIO9
  N22: Part1.GPIO25, Raspberry_Pi_1.GPIO25
  N23: Part1.SPI_CE0, Raspberry_Pi_1.GPIO8
  N24: Part1.EEDATA, Raspberry_Pi_1.ID_SD
  N25: Part1.EECLK, Raspberry_Pi_1.ID_SC
  N26: Part1.GPIO5, Raspberry_Pi_1.GPIO5
  N27: Part1.GPIO12, Raspberry_Pi_1.GPIO12
  N28: Part1.GPIO19, Raspberry_Pi_1.GPIO19
  N29: Part1.GPIO16, Raspberry_Pi_1.GPIO16
  N30: Part1.GPIO26, Raspberry_Pi_1.GPIO26
  N31: Part1.GPIO20, Raspberry_Pi_1.GPIO20
  N32: Part1.GPIO21, Raspberry_Pi_1.GPIO21
  N33: Part1.N$6, U1.3Y
  N34: Part1.N$9, U1.4Y
  5V: Part1.N$12#211, Part1.N$12#215, CONN1.5V, U1.VCC
  N35: Part1.N$49#312, Part1.N$55#342

notes:
  ~40cm

custom parts:
  Adafruit Perma-Proto HAT: To kick off the Adafruit HAT party, we have this Perma-Proto inspired plug in daughter board. It has a grid of 0.1" prototyping soldering holes for attaching chips, resistors, LED, potentiometers and more. The holes are connected underneath with traces to mimic the solderless breadboards you're familiar. There's also long power strips for +3V, +5V and Ground connections to the Pi. Near the top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
  74AHCT125: Quad Level-Shifter (3V to 5V) Quadruple Bus Buffer Gates With 3-State Outputs
